# Fritzing sketch plant_board_v01 (saved by Fritzing 0.9.3b)

parts:
  Part2 = Arduino Nano (Rev3.0)
  D_SENSE_1 = Diode [package=diode-1n4148]
  D_SENSE_2 = Diode [package=diode-1n4148]
  R_SENSE_2 = Resistor [tolerance=±5% resistance=20k package=THT]
  R_SENSE_1 = Resistor [tolerance=±5% resistance=20k package=THT]
  SENS_1 = screw terminal, 2 pins
  I2C_BUS = screw terminal, 2 pins
  R_TEMP_1 = Resistor [tolerance=±5% resistance=1k package=THT]
  pump_1 = screw terminal, 2 pins
  R1 = Resistor [tolerance=±5% resistance=10k package=THT]
  Q1 = NPN-Transistor [package="TO92 [THT]"]
  12V_input = screw terminal, 2 pins
  pump_2 = screw terminal, 2 pins
  Q2 = NPN-Transistor [package="TO92 [THT]"]
  R2 = Resistor [tolerance=±5% resistance=10k package=THT]
  D_SENSE_3 = Diode [package=diode-1n4148]
  D_SENSE_4 = Diode [package=diode-1n4148]
  R_SENSE_4 = Resistor [tolerance=±5% resistance=20k package=THT]
  R_SENSE_5 = Resistor [tolerance=±5% resistance=20k package=THT]
  SENS_2 = screw terminal, 2 pins
  LED1 = LED - 5mm [color="Green (565nm)" package="5 mm [THT]"]
  R_LED_1 = Resistor [tolerance=±5% resistance=150 package=THT]
  LED2 = LED - 5mm [color="Green (565nm)" package="5 mm [THT]"]
  R_LED_2 = Resistor [tolerance=±5% resistance=150 package=THT]
  DS2 = DS18B20 1-Wire Temperature Sensor [part_number=DS18B20]
  DS3 = DS18B20 1-Wire Temperature Sensor [part_number=DS18B20]

nets:
  GND: Part2.GND, R_SENSE_2.Pin_0, R_SENSE_1.Pin_0, Q1.E, 12V_input.pin2, Q2.E, R_SENSE_4.Pin_0, R_SENSE_5.Pin_0, R_LED_1.Pin_0, R_LED_2.Pin_0, DS2.GND, DS3.GND
  N1: Part2.D2, D_SENSE_2.A
  N2: Part2.D3, D_SENSE_1.A, LED2.anode
  N3: Part2.D4, D_SENSE_3.A
  N4: Part2.D5, D_SENSE_4.A, LED1.anode
  N5: Part2.D6, R2.Pin_0
  N6: Part2.D7, R1.Pin_0
  N7: Part2.D12/MISO, R_TEMP_1.Pin_1, DS2.DQ, DS3.DQ
  12V: Part2.VIN, pump_1.pin1, 12V_input.pin1, pump_2.pin1
  5V: Part2.5V, R_TEMP_1.Pin_0, DS2.VDD, DS3.VDD
  SCL (to D1): Part2.A5, I2C_BUS.pin1
  SDA (to D2): Part2.A4, I2C_BUS.pin2
  N8: Part2.A3, D_SENSE_2.C, R_SENSE_2.Pin_1, SENS_1.pin1
  N9: Part2.A2, D_SENSE_1.C, R_SENSE_1.Pin_1, SENS_1.pin2
  N10: Part2.A1, D_SENSE_3.C, R_SENSE_4.Pin_1, SENS_2.pin1
  N11: Part2.A0, D_SENSE_4.C, R_SENSE_5.Pin_1, SENS_2.pin2
  N12: pump_1.pin2, Q1.C
  N13: R1.Pin_1, Q1.B
  N14: pump_2.pin2, Q2.C
  N15: Q2.B, R2.Pin_1
  N16: LED1.cathode, R_LED_1.Pin_1
  N17: LED2.cathode, R_LED_2.Pin_1
